# Fritzing sketch complete circuit (saved by Fritzing 1.0.7)
circuit board: 6.48406cm x 2.99458cm
breadboards: 1

parts:
  R8 = Resistor [tolerance=±5% resistance=270 power=0.25W package=THT]
  C8 = Ceramic Capacitor [capacitance=10nF voltage=35V package="100 mil [THT, multilayer]"]
  R10 = Resistor [tolerance=±5% resistance=150 power=0.25W package=THT]
  R11 = Resistor [tolerance=±5% resistance=150 power=0.25W package=THT]
  C10 = Electrolytic Capacitor [capacitance=1µF voltage=35V package="100 mil [THT, electrolytic]"]
  C11 = Electrolytic Capacitor [capacitance=1µF voltage=35V package="100 mil [THT, electrolytic]"]
  R14 = Photocell (LDR) [power=0.25W dark_resistance_@0.01lx=300kΩ light_resistance_@100lx=400Ω luminance=10lx package=THT]
  R13 = Resistor [tolerance=±5% power=0.25W resistance=1k package=THT]
  R9 = Resistor [tolerance=±5% power=0.25W resistance=270 package=THT]
  C9 = Ceramic Capacitor [capacitance=10nF voltage=35V package="100 mil [THT, multilayer]"]
  OLED_I2C1 = OLED 128x64 I2C Monochrome Display
  J1 = female pin header, 20 pins [form="♀ (female)"]
  J2 = female pin header, 20 pins [form="♀ (female)"]
  R12 = Resistor [tolerance=±5% power=0.25W resistance=10k package=THT]
  C12 = Ceramic Capacitor [capacitance=100nF voltage=35V package="100 mil [THT, multilayer]"]
  SW1 = Header 2 [package=screwterminal-3.5mm-2_lock]
  JP1 = Header 4 [package=jst-4-pth]  # not connected
  C13 = Electrolytic Capacitor [capacitance=1µF voltage=35V package="100 mil [THT, electrolytic]"]
  J3 = female pin header, 1 pin [form="♀ (female)"]  # not connected
  J4 = female pin header, 1 pin [form="♀ (female)"]  # not connected
  J5 = female pin header, 1 pin [form="♀ (female)"]  # not connected
  J6 = female pin header, 1 pin [form="♀ (female)"]  # not connected
  J7 = female pin header, 1 pin [form="♀ (female)"]  # not connected
  J8 = female pin header, 1 pin [form="♀ (female)"]  # not connected
  J9 = female pin header, 1 pin [form="♀ (female)"]  # not connected
  J10 = female pin header, 1 pin [form="♀ (female)"]  # not connected
  J11 = female pin header, 1 pin [form="♀ (female)"]  # not connected
  J12 = female pin header, 1 pin [form="♀ (female)"]  # not connected

nets:
  N1: R8.Pin_0, J2.pin17
  N2: R8.Pin_1, C8.0, R10.Pin_0, C11.+
  N3: C8.1, R10.Pin_1, R11.Pin_0, C9.0, J1.pin3, J2.pin20, R12.Pin_1, C13.-
  N4: R11.Pin_1, C10.+, R9.Pin_1, C9.1
  N5: R14.pin_0, J1.pin19, C13.+
  N6: R14.pin_1, R13.Pin_1, J2.pin9
  N7: R13.Pin_0, C12.0, SW1.2
  N8: R9.Pin_0, J1.pin17
  N9: OLED_I2C1.connector4, J2.pin2
  N10: OLED_I2C1.connector5, J2.pin3
  N11: OLED_I2C1.connector7, J2.pin1
  N12: OLED_I2C1.connector8, J2.pin5
  N13: R12.Pin_0, C12.1, SW1.1
